// Logisim project full subtractor.circ as structural Verilog: 1 circuit, main circuit main
module main (
  input  in_1,
  input  in_2,
  input  in_3,
  input  in_4,
  input  in_5,
  input  in_6,
  input  in_7,
  input  in_8,
  input  in_9,
  input  in_10,
  input  in_11,
  input  in_12,
  input  in_13,
  input  in_14,
  input  in_15,
  input  in_16,
  input  in_17,
  input  in_18,
  input  in_19,
  input  in_20,
  input  in_21,
  input  in_22,
  input  in_23,
  input  in_24,
  output out_25,
  output out_26,
  output out_27,
  output out_28,
  output out_29,
  output out_30,
  output out_31,
  output out_32,
  output out_33,
  output out_34,
  output out_35,
  output out_36,
  output out_37,
  output out_38,
  output out_39,
  output out_40
);

  wire and_1_out, and_2_out, and_3_out, and_4_out, and_5_out, and_6_out, and_7_out, and_8_out, and_9_out,
       and_10_out, and_11_out, and_12_out, and_13_out, and_14_out, and_15_out, and_16_out, not_1_out,
       not_2_out, not_3_out, not_4_out, not_5_out, not_6_out, not_7_out, not_8_out, not_9_out, not_10_out,
       not_11_out, not_12_out, not_13_out, not_14_out, not_15_out, not_16_out, xor_1_out, xor_2_out,
       xor_3_out, xor_4_out, xor_9_out, xor_10_out, xor_11_out, xor_15_out;

  xor xor_1 (xor_1_out, in_3, in_5);
  not not_1 (not_1_out, in_3);
  xor xor_2 (xor_2_out, in_9, in_11);
  not not_2 (not_2_out, in_9);
  xor xor_3 (xor_3_out, in_15, in_17);
  not not_3 (not_3_out, in_15);
  xor xor_4 (xor_4_out, in_20, in_22);
  not not_4 (not_4_out, in_20);
  not not_5 (not_5_out, xor_1_out);
  and and_1 (and_1_out, not_1_out, in_5);
  not not_6 (not_6_out, xor_2_out);
  and and_2 (and_2_out, not_2_out, in_11);
  not not_7 (not_7_out, xor_3_out);
  and and_3 (and_3_out, not_3_out, in_17);
  and and_4 (and_4_out, not_4_out, in_22);
  xor xor_5 (out_25, in_1, xor_1_out);
  xor xor_6 (out_29, in_7, xor_2_out);
  xor xor_7 (out_33, in_13, xor_3_out);
  xor xor_8 (out_37, in_19, xor_4_out);
  not not_8 (not_8_out, xor_4_out);
  and and_5 (and_5_out, not_5_out, in_1);
  and and_6 (and_6_out, not_6_out, in_7);
  and and_7 (and_7_out, not_7_out, in_13);
  and and_8 (and_8_out, not_8_out, in_19);
  or or_1 (out_27, and_5_out, and_1_out);
  or or_2 (out_31, and_6_out, and_2_out);
  or or_3 (out_35, and_7_out, and_3_out);
  or or_4 (out_39, and_8_out, and_4_out);
  xor xor_9 (xor_9_out, in_4, in_6);
  not not_9 (not_9_out, in_4);
  xor xor_10 (xor_10_out, in_10, in_12);
  not not_10 (not_10_out, in_10);
  and and_9 (and_9_out, not_9_out, in_6);
  and and_10 (and_10_out, not_10_out, in_12);
  xor xor_11 (xor_11_out, in_16, in_18);
  not not_11 (not_11_out, in_16);
  xor xor_12 (out_26, in_2, xor_9_out);
  not not_12 (not_12_out, xor_9_out);
  xor xor_13 (out_30, in_8, xor_10_out);
  not not_13 (not_13_out, xor_10_out);
  and and_11 (and_11_out, not_11_out, in_18);
  not not_14 (not_14_out, in_23);
  xor xor_14 (out_34, in_14, xor_11_out);
  not not_15 (not_15_out, xor_11_out);
  xor xor_15 (xor_15_out, in_23, in_24);
  and and_12 (and_12_out, not_12_out, in_2);
  and and_13 (and_13_out, not_13_out, in_8);
  and and_14 (and_14_out, not_14_out, in_24);
  or or_5 (out_28, and_12_out, and_9_out);
  or or_6 (out_32, and_13_out, and_10_out);
  and and_15 (and_15_out, not_15_out, in_14);
  xor xor_16 (out_38, in_21, xor_15_out);
  not not_16 (not_16_out, xor_15_out);
  or or_7 (out_36, and_15_out, and_11_out);
  and and_16 (and_16_out, not_16_out, in_21);
  or or_8 (out_40, and_16_out, and_14_out);
endmodule
