// Logisim project half subtractor.circ as structural Verilog: 1 circuit, main circuit main
module main (
  input  in_1,
  input  in_2,
  input  in_3,
  input  in_4,
  input  in_5,
  input  in_6,
  input  in_7,
  input  in_8,
  output out_9,
  output out_10,
  output out_11,
  output out_12,
  output out_13,
  output out_14,
  output out_15,
  output out_16
);

  wire not_1_out, not_2_out, not_3_out, not_4_out;

  xor xor_1 (out_9, in_1, in_3);
  not not_1 (not_1_out, in_1);
  xor xor_2 (out_13, in_5, in_7);
  not not_2 (not_2_out, in_5);
  and and_1 (out_15, not_2_out, in_7);
  and and_2 (out_11, not_1_out, in_3);
  not not_3 (not_3_out, in_2);
  not not_4 (not_4_out, in_6);
  xor xor_3 (out_10, in_2, in_4);
  xor xor_4 (out_14, in_6, in_8);
  and and_3 (out_12, not_3_out, in_4);
  and and_4 (out_16, not_4_out, in_8);
endmodule
